# Fritzing sketch MyLifeIsPatate (saved by Fritzing 0.9.3b)
breadboards: 1

parts:
  Resistance_3 = Resistor [tolerance=±5% resistance=1M package=THT]
  Resistance_2 = Resistor [tolerance=±5% resistance=3.3k package="0603 [SMD]"]
  DEL_Red = LED - 5mm [color="Red (633nm)" package="5 mm [THT]"]
  Condo_2 = Capacitor [package=cap-pth-small]
  Condo_1 = Capacitor [package=cap-pth-small]
  Composant1 = Arduino Uno (Rev3) - ICSP
  Resistance_1 = Resistor [tolerance=±5% resistance=10k package="0603 [SMD]"]
  L1 = Inductor [package="1206 [SMD]"]
  Pomme_de_terre = Capacitor [package=cap-pth-small]

nets:
  N1: Resistance_3.Pin_0, Resistance_2.Pin_1, Condo_2.1, Composant1.GND, Pomme_de_terre.1
  N2: Resistance_3.Pin_1, DEL_Red.cathode, Condo_2.2, Composant1.A0
  N3: Resistance_2.Pin_0, Resistance_1.Pin_0, L1.pin_1
  N4: DEL_Red.anode, Condo_1.2, L1.pin_0
  N5: Condo_1.1, Pomme_de_terre.2
  N6: Composant1.D9_PWM, Resistance_1.Pin_1
