# Fritzing sketch MyLifeIsPatate (saved by Fritzing 0.9.2b)
circuit board: 5.78986cm x 5.5711cm
breadboards: 1

parts:
  Arduino = Arduino BT
  R2 = Resistor [tolerance=±5% resistance=220 package="0805 [SMD]"]
  L1 = Inductor [package="400 mil [THT]"]
  C1 = Ceramic Capacitor [capacitance=10nF package="1206 [SMD, multilayer]"]
  D1 = Rectifier Diode [part_number=1N4001 package="Melf DO-213 AB [SMD]"]
  R1 = Resistor [tolerance=±5% resistance=10k package="0805 [SMD]"]
  C2 = Ceramic Capacitor [capacitance=10nF package="1206 [SMD, multilayer]"]
  VERRE_D'EAU = TOUCH [package=touch2]
  LED1 = smd LED [color="Orange (620nm)" package="0805 [SMD]"]
  LED2 = smd LED [color="Green (555nm)" package="0805 [SMD]"]
  LED3 = smd LED [color="Blue (430nm)" package="0805 [SMD]"]
  R3 = Resistor [tolerance=±5% resistance=220 package="0805 [SMD]"]
  R4 = Resistor [tolerance=±5% resistance=220 package="0805 [SMD]"]
  R5 = Resistor [tolerance=±5% resistance=220 package="0805 [SMD]"]
  R6 = Resistor [tolerance=±5% resistance=3.3k package="0805 [SMD]"]

nets:
  N1: Arduino.MISO, Arduino.MISO/D12, LED3.anode
  N2: Arduino.MOSI, Arduino.MOSI/PWM_D11, LED2.anode
  N3: Arduino.PWM_D9, R1.Pin_0
  N4: Arduino.SS/PWM_D10, LED1.anode
  N5: Arduino.GND, R2.Pin_0, C2.1, R3.Pin_0, R4.Pin_0, R5.Pin_0, R6.Pin_0
  N6: Arduino.A0, R2.Pin_1, D1.cathode, C2.0
  N7: L1.pin_0, R1.Pin_1, R6.Pin_1
  N8: L1.pin_1, C1.0, D1.anode
  N9: C1.1, VERRE_D'EAU.T2
  N10: LED1.cathode, R3.Pin_1
  N11: LED2.cathode, R4.Pin_1
  N12: LED3.cathode, R5.Pin_1
